# Fritzing sketch dumbSmartSwitchBread (saved by Fritzing 0.9.3b)
breadboards: 1

parts:
  Part1 = Arduino Nano 33 IOT
  J1 = Basic Servo
  ZS-042_RTC1 = ZS-042 RTC Module

nets:
  N1: Part1.RESET, Part1.A7
  GND: Part1.GND, Part1.D13~, J1.gnd, ZS-042_RTC1.GND
  N2: Part1.D2, J1.pulse
  N3: Part1.D11/MOSI, Part1.+5V
  N4: Part1.A5, ZS-042_RTC1.SCL
  N5: Part1.A4, ZS-042_RTC1.SDA
  VCC: Part1.3V3, J1.vcc, ZS-042_RTC1.VCC

custom parts:
  Arduino Nano 33 IOT: The Arduino Nano 33 IoT is the easiest and cheapest point of entry to enhance existing devices (and creating new ones) to be part of the IoT and designing pico-network applications. Whether you are looking at building a sensor network connected to your office or home router, or if you want to create a BLE device sending data to a cellphone, the Nano 33 IoT is your one-stop-solution for many of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
